// Digital circuit Clock Conversion Module.dig as structural Verilog
module Clock_Conversion_Module (
  input  CLK_IN,
  input  B,
  input  A,
  output CLK_OUT
);

  wire jk_ff_1_q, jk_ff_2_q, jk_ff_3_q, jk_ff_4_q;

  JK_FF jk_ff_1 (.J(1'b1), .C(CLK_IN), .K(1'b1), .Q(jk_ff_1_q));  // open: nQ
  JK_FF jk_ff_2 (.J(1'b1), .C(jk_ff_1_q), .K(1'b1), .Q(jk_ff_2_q));  // open: nQ
  JK_FF jk_ff_3 (.J(1'b1), .C(jk_ff_2_q), .K(1'b1), .Q(jk_ff_3_q));  // open: nQ
  JK_FF jk_ff_4 (.J(1'b1), .C(jk_ff_3_q), .K(1'b1), .Q(jk_ff_4_q));  // open: nQ
  Multiplexer #(.Selector_Bits(2)) multiplexer_1 (
    .sel({A, B}), .in_0(jk_ff_1_q), .in_1(jk_ff_2_q), .in_2(jk_ff_3_q), .in_3(jk_ff_4_q), .out(CLK_OUT));

  // Notes on the sheet:
  //   B: default 1
endmodule

/* Test case Test Q4:
#TEST CASE
CLK_IN	A	B	CLK_OUT
1	0	1	1
0	0	1	1
1	0	1	1
0	0	1	1
1	0	1	0
0	0	1	0
1	0	1	0
0	0	1	0
1	0	1	1
0	0	1	1
1	0	1	1
0	0	1	1
1	0	1	0
0	0	1	0
1	0	1	0
0	0	1	0
1	0	1	1
0	0	1	1
1	0	1	1
0	0	1	1
1	0	1	0
0	0	1	0
1	0	1	0
0	0	1	0
1	0	1	1
0	0	1	1
1	0	1	1
0	0	1	1
1	0	1	0
0	0	1	0
1	0	1	0
0	0	1	0
*/
