// Digital circuit Display Buffer Module.dig as structural Verilog
module Display_Buffer_Module (
  input  [15:0] SEG_IN,
  input  CLK,
  input  DISP_EN,
  output [15:0] BUF_OUT
);

  Seven_Seg seven_seg_1 (
    .a(BUF_OUT[8]), .b(BUF_OUT[9]), .c(BUF_OUT[10]), .d(BUF_OUT[11]), .e(BUF_OUT[12]), .f(BUF_OUT[13]),
    .g(BUF_OUT[14]), .dp(BUF_OUT[15]));
  Seven_Seg seven_seg_2 (
    .a(BUF_OUT[0]), .b(BUF_OUT[1]), .c(BUF_OUT[2]), .d(BUF_OUT[3]), .e(BUF_OUT[4]), .f(BUF_OUT[5]),
    .g(BUF_OUT[6]), .dp(BUF_OUT[7]));
  Register #(.Bits(16)) Reg (.D(SEG_IN), .C(CLK), .en(DISP_EN), .Q(BUF_OUT));
endmodule

/* Test case TEST:
SEG_IN				CLK	DISP_EN	BUF_OUT
0000011101101111		0	0	0
0111111100111111		1	1	0111111100111111		
0000011000000110		0	1	0111111100111111	
0110110101111101		1	0	0111111100111111	
0110110101111100		0	1	0111111100111111	
0110110101111110		1	1	0110110101111110		
0110110101111001		0	0	0110110101111110		
1110110111100001		1	1	1110110111100001		
0000011101101111		0	0	1110110111100001	
0110111100000111		1	1	0110111100000111		
1111111101101111		0	1	0110111100000111	
*/
