// Digital circuit Full Circuit.dig as structural Verilog
module Full_Circuit (
  input  START,
  input  SERIAL_IN,
  input  CLK_IN,
  input  B,
  input  A,
  output [15:0] OUT
);

  wire clock_conversion_module_1_clk_out, serial_to_paralle_module_1_disp_en;
  wire [15:0] serial_to_paralle_module_1_seg_out;

  Seven_Seg seven_seg_1 (
    .a(OUT[8]), .b(OUT[9]), .c(OUT[10]), .d(OUT[11]), .e(OUT[12]), .f(OUT[13]), .g(OUT[14]), .dp(OUT[15]));
  Seven_Seg seven_seg_2 (
    .a(OUT[0]), .b(OUT[1]), .c(OUT[2]), .d(OUT[3]), .e(OUT[4]), .f(OUT[5]), .g(OUT[6]), .dp(OUT[7]));
  Clock_Conversion_Module clock_conversion_module_1 (
    .CLK_IN(CLK_IN), .B(B), .A(A), .CLK_OUT(clock_conversion_module_1_clk_out));
  Display_Buffer_Module display_buffer_module_1 (
    .SEG_IN(serial_to_paralle_module_1_seg_out), .CLK(CLK_IN), .DISP_EN(serial_to_paralle_module_1_disp_en),
    .BUF_OUT(OUT));
  Serial_To_Paralle_Module serial_to_paralle_module_1 (
    .CLK_OUT(clock_conversion_module_1_clk_out), .START(START), .SERIAL_IN(SERIAL_IN),
    .SEG_OUT(serial_to_paralle_module_1_seg_out), .DISP_EN(serial_to_paralle_module_1_disp_en));
endmodule

/* Test case TEST:
CLK_IN	A	B	START	SERIAL_IN	OUT
1 	0 	1 	0 	1		0x3F3F
0 	0 	1 	0 	1		0x3F3F
1 	0 	1 	0 	1		0x3F3F
0 	0 	1 	0 	1		0x3F3F
1 	0 	1 	0 	0		0x3F3F
0 	0 	1 	0 	0		0x3F3F
1 	0 	1 	0 	0		0x3F3F
0 	0 	1 	0 	0		0x3F3F
1 	0 	1 	0 	0		0x3F3F
0 	0 	1 	0 	0		0x3F3F
1 	0 	1 	0 	0		0x3F3F
0 	0 	1 	0 	0		0x3F3F
1 	0 	1 	0 	0		0x3F3F
0 	0 	1 	0 	0		0x3F3F
1 	0 	1 	0 	0		0x3F3F
0 	0 	1 	0 	0		0x3F3F
1 	0 	1 	0 	0		0x3F3F
0 	0 	1 	0 	0		0x3F3F
1 	0 	1 	0 	0		0x3F3F
0 	0 	1 	0 	0		0x3F3F
1 	0 	1 	0 	0		0x3F3F
0 	0 	1 	0 	0		0x3F3F
1 	0 	1 	0 	0		0x3F3F
0 	0 	1 	0 	0		0x3F3F
1 	0 	1 	0 	1		0x3F3F
0 	0 	1 	0 	1		0x3F3F
1 	0 	1 	0 	1		0x3F3F
0 	0 	1 	0 	1		0x3F3F
1 	0 	1 	0 	0		0x3F3F
0 	0 	1 	0 	0		0x3F3F
1 	0 	1 	0 	0		0x3F3F
0 	0 	1 	0 	0		0x3F3F
1 	0 	1 	0 	0		0x3F3F
0 	0 	1 	0 	0		0x3F3F
1 	0 	1 	0 	0		0x3F3F
0 	0 	1 	0 	0		0x3F3F
1 	0 	1 	0 	0		0x3F3F
0 	0 	1	0 	0		0x3F3F
1 	0 	1 	0 	0		0x3F3F
0 	0 	1	0 	0		0x3F3F
1 	0 	1 	0 	1		0x3F3F
0 	0 	1	0 	1		0x3F3F
1 	0 	1 	0 	1		0x3F3F
0 	0 	1	0 	1		0x3F3F
1 	0 	1	0 	0		0x3F3F
0 	0 	1 	0 	0		0x3F3F
1 	0 	1	0 	0		0x3F3F
0 	0 	1 	0 	0		0x3F3F
1	0 	1 	0 	1		0x3F3F
0 	0 	1 	0 	1		0x3F3F
1	0 	1 	0 	1		0x3F3F
0 	0 	1 	0 	1		0x3F3F
1 	0 	1 	0 	0		0x3F3F
0 	0 	1 	0 	0		0x3F3F
1 	0 	1 	0 	0		0x3F3F
0 	0 	1 	0 	0		0x3F3F
1 	0 	1 	0 	1		0x3F3F
0 	0 	1 	0 	1		0x3F3F
1 	0 	1 	0 	1		0x6F07
0 	0 	1 	0 	1		0x6F07
*/
