// Digital circuit Serial To Paralle Module.dig as structural Verilog
module Serial_To_Paralle_Module (
  input  CLK_OUT,
  input  START,
  input  SERIAL_IN,
  output [15:0] SEG_OUT,
  output DISP_EN
);

  wire _74164_1_pin3, _74164_1_pin4, _74164_1_pin5, _74164_1_pin6, _74164_1_pin9, _74164_1_pin10,
       _74164_1_pin11, _74164_1_pin12, _74164_1_pin13;

  LookUpTable #(.Bits(8)) LUT1 (
    .in0(_74164_1_pin3), .in1(_74164_1_pin4), .in2(_74164_1_pin5), .in3(_74164_1_pin6), .out(SEG_OUT[7:0]));
  _74164 _74164_1 (
    .pin1(SERIAL_IN), .pin2(SERIAL_IN), .pin3(_74164_1_pin3), .pin4(_74164_1_pin4), .pin5(_74164_1_pin5),
    .pin6(_74164_1_pin6), .pin7(1'b0), .pin8(CLK_OUT), .pin9(_74164_1_pin9), .pin10(_74164_1_pin10),
    .pin11(_74164_1_pin11), .pin12(_74164_1_pin12), .pin13(_74164_1_pin13), .pin14(1'b1));
  LookUpTable #(.Bits(8)) LUT3 (
    .in0(_74164_1_pin10), .in1(_74164_1_pin11), .in2(_74164_1_pin12), .in3(_74164_1_pin13),
    .out(SEG_OUT[15:8]));
  not not_1 (_74164_1_pin9, START);
  COUNTER counter_1 (.CLK(CLK_OUT), .DISP_EN(DISP_EN));

  // Notes on the sheet:
  //   contents of LUT1 (hex, n*v repeats v):
  //   3f,6,5b,4f,66,6d,7d,7,7f,6f,80,80,80,80,80,80
  //   contents of LUT3 (hex, n*v repeats v):
  //   3f,6,5b,4f,66,6d,7d,7,7f,6f,80,80,80,80,80,80
endmodule

/* Test case TEST:
CLK_OUT	START	SERIAL_IN	SEG_OUT			DISP_EN
1 	0 	1		0x3F3F			0
0 	0 	1		0x3F3F			0
1 	0 	0		0x3F06			0	
0 	0 	0		0x3F06			0
1 	0 	0		0x3F5B			0	
0 	0 	0		0x3F5B			0
1 	0 	1		0x3F66			0
0 	0 	1		0x3F66			0
1	0	0		0x3F6F			0
0 	0 	0		0x3F6F			0
1 	0 	1		0x65B			0	
0 	0 	1		0x65B			0	
1 	0 	1		0x5B6D			0	
0 	0 	1		0x5B6D			0	
1 	0 	1		0x6680			1	
0 	0 	1		0x6680			1
1 	0 	0		0x6F07			0	
*/
